// Logisim project CPU.circ as structural Verilog
module halfAdder (
  input  A,
  input  B,
  input  CarryIn,
  output Sum,
  output CarryOut
);

  wire and_1_out, and_2_out, or_1_out;

  xor xor_1 (Sum, A, B, CarryIn);
  and and_1 (and_1_out, A, B);
  or or_1 (or_1_out, A, B);
  and and_2 (and_2_out, or_1_out, CarryIn);
  or or_2 (CarryOut, and_1_out, and_2_out);
endmodule

module fullAdder8 (
  input  [7:0] A,
  input  [7:0] B,
  input  CarryIn,
  output [7:0] Sum,
  output CarryOut
);

  wire halfadder_1_carryout, halfadder_2_carryout, halfadder_3_carryout, halfadder_4_carryout,
       halfadder_5_carryout, halfadder_6_carryout, halfadder_7_carryout;

  halfAdder halfadder_1 (.A(A[0]), .B(B[0]), .CarryIn(CarryIn), .Sum(Sum[0]), .CarryOut(halfadder_1_carryout));
  halfAdder halfadder_2 (
    .A(A[1]), .B(B[1]), .CarryIn(halfadder_1_carryout), .Sum(Sum[1]), .CarryOut(halfadder_2_carryout));
  halfAdder halfadder_3 (
    .A(A[2]), .B(B[2]), .CarryIn(halfadder_2_carryout), .Sum(Sum[2]), .CarryOut(halfadder_3_carryout));
  halfAdder halfadder_4 (
    .A(A[3]), .B(B[3]), .CarryIn(halfadder_3_carryout), .Sum(Sum[3]), .CarryOut(halfadder_4_carryout));
  halfAdder halfadder_5 (
    .A(A[4]), .B(B[4]), .CarryIn(halfadder_4_carryout), .Sum(Sum[4]), .CarryOut(halfadder_5_carryout));
  halfAdder halfadder_6 (
    .A(A[5]), .B(B[5]), .CarryIn(halfadder_5_carryout), .Sum(Sum[5]), .CarryOut(halfadder_6_carryout));
  halfAdder halfadder_7 (
    .A(A[6]), .B(B[6]), .CarryIn(halfadder_6_carryout), .Sum(Sum[6]), .CarryOut(halfadder_7_carryout));
  halfAdder halfadder_8 (.A(A[7]), .B(B[7]), .CarryIn(halfadder_7_carryout), .Sum(Sum[7]), .CarryOut(CarryOut));
endmodule

module integerAdder8 (
  input  [7:0] A,
  input  [7:0] B,
  input  CarryIn,
  output [7:0] Sum,
  output CarryOut
);

  fullAdder8 fulladder8_1 (.A(A), .B(B), .CarryIn(CarryIn), .Sum(Sum), .CarryOut(CarryOut));
endmodule

module integerMultiply8 (
  input  [7:0] A,
  input  [7:0] B,
  output [7:0] Product,
  output Overflow
);

  wire fulladder8_1_carryout, fulladder8_2_carryout, fulladder8_3_carryout, fulladder8_4_carryout,
       fulladder8_5_carryout, fulladder8_6_carryout, fulladder8_7_carryout;
  wire [7:0] fulladder8_1_sum, fulladder8_2_sum, fulladder8_3_sum, fulladder8_4_sum, fulladder8_5_sum,
       fulladder8_6_sum, fulladder8_7_sum, xor8_1_o, xor8_2_o, xor8_3_o, xor8_4_o, xor8_5_o, xor8_6_o,
       xor8_7_o, xor8_8_o;

  xor8 xor8_1 (.A(A), .B({8{B[0]}}), .O(xor8_1_o));
  xor8 xor8_2 (.A(A), .B({8{B[1]}}), .O(xor8_2_o));
  xor8 xor8_3 (.A(A), .B({8{B[2]}}), .O(xor8_3_o));
  xor8 xor8_4 (.A(A), .B({8{B[3]}}), .O(xor8_4_o));
  xor8 xor8_5 (.A(A), .B({8{B[4]}}), .O(xor8_5_o));
  xor8 xor8_6 (.A(A), .B({8{B[5]}}), .O(xor8_6_o));
  xor8 xor8_7 (.A(A), .B({8{B[6]}}), .O(xor8_7_o));
  xor8 xor8_8 (.A(A), .B({8{B[7]}}), .O(xor8_8_o));
  fullAdder8 fulladder8_1 (
    .A(A), .B(xor8_1_o), .Sum(fulladder8_1_sum), .CarryOut(fulladder8_1_carryout));  // open: CarryIn
  fullAdder8 fulladder8_2 (
    .A(fulladder8_1_sum), .B(xor8_2_o), .CarryIn(fulladder8_1_carryout), .Sum(fulladder8_2_sum),
    .CarryOut(fulladder8_2_carryout));
  fullAdder8 fulladder8_3 (
    .A(fulladder8_2_sum), .B(xor8_3_o), .CarryIn(fulladder8_2_carryout), .Sum(fulladder8_3_sum),
    .CarryOut(fulladder8_3_carryout));
  fullAdder8 fulladder8_4 (
    .A(fulladder8_3_sum), .B(xor8_4_o), .CarryIn(fulladder8_3_carryout), .Sum(fulladder8_4_sum),
    .CarryOut(fulladder8_4_carryout));
  fullAdder8 fulladder8_5 (
    .A(fulladder8_4_sum), .B(xor8_5_o), .CarryIn(fulladder8_4_carryout), .Sum(fulladder8_5_sum),
    .CarryOut(fulladder8_5_carryout));
  fullAdder8 fulladder8_6 (
    .A(fulladder8_5_sum), .B(xor8_6_o), .CarryIn(fulladder8_5_carryout), .Sum(fulladder8_6_sum),
    .CarryOut(fulladder8_6_carryout));
  fullAdder8 fulladder8_7 (
    .A(fulladder8_6_sum), .B(xor8_7_o), .CarryIn(fulladder8_6_carryout), .Sum(fulladder8_7_sum),
    .CarryOut(fulladder8_7_carryout));
  fullAdder8 fulladder8_8 (
    .A(fulladder8_7_sum), .B(xor8_8_o), .CarryIn(fulladder8_7_carryout), .Sum(Product), .CarryOut(Overflow));
endmodule

module xor8 (
  input  [7:0] A,
  input  [7:0] B,
  output [7:0] O
);

  xor xor_1 (O[0], A[0], B[0]);
  xor xor_2 (O[1], A[1], B[1]);
  xor xor_3 (O[2], A[2], B[2]);
  xor xor_4 (O[3], A[3], B[3]);
  xor xor_5 (O[4], A[4], B[4]);
  xor xor_6 (O[5], A[5], B[5]);
  xor xor_7 (O[6], A[6], B[6]);
  xor xor_8 (O[7], A[7], B[7]);
endmodule

module and8 (
  input  [7:0] A,
  input  [7:0] B,
  output [7:0] O
);

  and and_1 (O[0], A[0], B[0]);
  and and_2 (O[1], A[1], B[1]);
  and and_3 (O[2], A[2], B[2]);
  and and_4 (O[3], A[3], B[3]);
  and and_5 (O[4], A[4], B[4]);
  and and_6 (O[5], A[5], B[5]);
  and and_7 (O[6], A[6], B[6]);
  and and_8 (O[7], A[7], B[7]);
endmodule

module or8 (
  input  [7:0] A,
  input  [7:0] B,
  output [7:0] O
);

  or or_1 (O[0], A[0], B[0]);
  or or_2 (O[1], A[1], B[1]);
  or or_3 (O[2], A[2], B[2]);
  or or_4 (O[3], A[3], B[3]);
  or or_5 (O[4], A[4], B[4]);
  or or_6 (O[5], A[5], B[5]);
  or or_7 (O[6], A[6], B[6]);
  or or_8 (O[7], A[7], B[7]);
endmodule

module buf8 (
  input  [7:0] A,
  output [7:0] O
);


  assign O = A;
endmodule

module integerDivide8 (
  input  [7:0] A,
  input  [7:0] B
);
endmodule

module lshft8 (
  input  [7:0] A,
  output [7:0] O
);


  assign O = {A[6:0], A[7]};
endmodule

module rshft8 (
  input  [7:0] A,
  output [7:0] O
);


  assign O = {A[0], A[7:1]};
endmodule

module TEMP (
  input  [7:0] A,
  input  [7:0] B,
  output [7:0] Lower8,
  output Overflow
);

  wire fulladder8_1_carryout, fulladder8_2_carryout, fulladder8_3_carryout, fulladder8_4_carryout,
       fulladder8_5_carryout, fulladder8_6_carryout;
  wire [7:0] and8_1_o, and8_2_o, and8_3_o, and8_4_o, and8_5_o, and8_6_o, and8_7_o, and8_8_o,
       fulladder8_1_sum, fulladder8_2_sum, fulladder8_3_sum, fulladder8_4_sum, fulladder8_5_sum,
       fulladder8_6_sum, lshft8_trunc_1_o, lshft8_trunc_2_o, lshft8_trunc_3_o, lshft8_trunc_4_o,
       lshft8_trunc_5_o, lshft8_trunc_6_o, lshft8_trunc_7_o, lshft8_trunc_8_o, lshft8_trunc_9_o,
       lshft8_trunc_10_o, rshft8_trunc_1_o, rshft8_trunc_2_o, rshft8_trunc_3_o, rshft8_trunc_4_o,
       rshft8_trunc_5_o, rshft8_trunc_6_o;

  and8 and8_1 (.A(A), .B({8{B[0]}}), .O(and8_1_o));
  and8 and8_2 (.A(A), .B({8{B[1]}}), .O(and8_2_o));
  and8 and8_3 (.A(A), .B({8{B[2]}}), .O(and8_3_o));
  and8 and8_4 (.A(A), .B({8{B[3]}}), .O(and8_4_o));
  and8 and8_5 (.A(A), .B({8{B[4]}}), .O(and8_5_o));
  and8 and8_6 (.A(A), .B({8{B[5]}}), .O(and8_6_o));
  and8 and8_7 (.A(A), .B({8{B[6]}}), .O(and8_7_o));
  and8 and8_8 (.A(A), .B({8{B[7]}}), .O(and8_8_o));
  lshft8_trunc lshft8_trunc_1 (.A(and8_2_o), .O(lshft8_trunc_1_o));
  lshft8_trunc lshft8_trunc_2 (.A(and8_3_o), .O(lshft8_trunc_2_o));
  lshft8_trunc lshft8_trunc_3 (.A(and8_4_o), .O(lshft8_trunc_3_o));
  lshft8_trunc lshft8_trunc_4 (.A(and8_5_o), .O(lshft8_trunc_4_o));
  rshft8_trunc rshft8_trunc_1 (.A(and8_6_o), .O(rshft8_trunc_1_o));
  rshft8_trunc rshft8_trunc_2 (.A(and8_7_o), .O(rshft8_trunc_2_o));
  rshft8_trunc rshft8_trunc_3 (.A(and8_8_o), .O(rshft8_trunc_3_o));
  lshft8_trunc lshft8_trunc_5 (.A(lshft8_trunc_2_o), .O(lshft8_trunc_5_o));
  lshft8_trunc lshft8_trunc_6 (.A(lshft8_trunc_3_o), .O(lshft8_trunc_6_o));
  lshft8_trunc lshft8_trunc_7 (.A(lshft8_trunc_4_o), .O(lshft8_trunc_7_o));
  rshft8_trunc rshft8_trunc_4 (.A(rshft8_trunc_1_o), .O(rshft8_trunc_4_o));
  rshft8_trunc rshft8_trunc_5 (.A(rshft8_trunc_2_o), .O(rshft8_trunc_5_o));
  lshft8_trunc lshft8_trunc_8 (.A(lshft8_trunc_6_o), .O(lshft8_trunc_8_o));
  lshft8_trunc lshft8_trunc_9 (.A(lshft8_trunc_7_o), .O(lshft8_trunc_9_o));
  rshft8_trunc rshft8_trunc_6 (.A(rshft8_trunc_4_o), .O(rshft8_trunc_6_o));
  lshft8_trunc lshft8_trunc_10 (.A(lshft8_trunc_9_o), .O(lshft8_trunc_10_o));
  fullAdder8 fulladder8_1 (
    .A(and8_1_o), .B(lshft8_trunc_1_o), .Sum(fulladder8_1_sum), .CarryOut(fulladder8_1_carryout));  // open: CarryIn
  fullAdder8 fulladder8_2 (
    .A(fulladder8_1_sum), .B(lshft8_trunc_5_o), .CarryIn(fulladder8_1_carryout), .Sum(fulladder8_2_sum),
    .CarryOut(fulladder8_2_carryout));
  fullAdder8 fulladder8_3 (
    .A(fulladder8_2_sum), .B(lshft8_trunc_8_o), .CarryIn(fulladder8_2_carryout), .Sum(fulladder8_3_sum),
    .CarryOut(fulladder8_3_carryout));
  fullAdder8 fulladder8_4 (
    .A(fulladder8_3_sum), .B(lshft8_trunc_10_o), .CarryIn(fulladder8_3_carryout), .Sum(fulladder8_4_sum),
    .CarryOut(fulladder8_4_carryout));
  fullAdder8 fulladder8_5 (
    .A(fulladder8_4_sum), .B(rshft8_trunc_6_o), .CarryIn(fulladder8_4_carryout), .Sum(fulladder8_5_sum),
    .CarryOut(fulladder8_5_carryout));
  fullAdder8 fulladder8_6 (
    .A(fulladder8_5_sum), .B(rshft8_trunc_5_o), .CarryIn(fulladder8_5_carryout), .Sum(fulladder8_6_sum),
    .CarryOut(fulladder8_6_carryout));
  fullAdder8 fulladder8_7 (
    .A(fulladder8_6_sum), .B(rshft8_trunc_3_o), .CarryIn(fulladder8_6_carryout), .Sum(Lower8),
    .CarryOut(Overflow));

  // Notes on the sheet:
  //   1000 0001 x 0000 00010 =
  //   Upper = 0000 0001
  //   Lower = 0000 0010
endmodule

module lshft8_trunc (
  input  [7:0] A,
  output [7:0] O
);

  not not_1 (O[0], 1'b1);

  assign O[7:1] = A[6:0];
endmodule

module rshft8_trunc (
  input  [7:0] A,
  output [7:0] O
);

  not not_1 (O[7], 1'b1);

  assign O[6:0] = A[7:1];
endmodule
